# Fritzing sketch Usage (saved by Fritzing 0.9.2b)
breadboards: 1

parts:
  Q1 = Basic FET P-Channel [package="TO220 [THT]"]
  R1 = Resistor [tolerance=±5% resistance=10k package=THT]
  12V_LED_STRIPE = LED - 5mm [color="Red (633nm)" package="5 mm [THT]"]
  Arduino_output/input_switch = Pushbutton [package=THT]

nets:
  N1: Q1.gate, R1.Pin_1, Arduino_output/input_switch.leg1
  N2: Q1.drain, 12V_LED_STRIPE.cathode
  GND: Q1.source, Arduino_output/input_switch.leg0
  12V: R1.Pin_0, 12V_LED_STRIPE.anode
